# Fritzing sketch HardwareBoardGraphic (saved by Fritzing 0.9.10b)
circuit board: 8.46667cm x 5.64444cm
breadboards: 1

parts:
  元件1 = Arduino Uno (Rev3)
  LED1 = LED - 3mm [color="Red (633nm)" current=0.030 package="3 mm [THT]"]
  LED2 = LED - 3mm [color="Blue (470nm)" current=0.030 package="3 mm [THT]"]
  LED3 = LED - 3mm [color="Green (565nm)" current=0.030 package="3 mm [THT]"]
  LED4 = LED - 3mm [color="Yellow (585nm)" current=0.030 package="3 mm [THT]"]
  LED5 = LED - 3mm [color="White (8000K)" current=0.030 package="3 mm [THT]"]
  LED6 = LED - 3mm [color="Blue (470nm)" current=0.030 package="3 mm [THT]"]
  LED7 = LED - 3mm [color="Blue (470nm)" current=0.030 package="3 mm [THT]"]
  LED8 = LED - 3mm [color="Blue (470nm)" current=0.030 package="3 mm [THT]"]
  LED9 = LED - 3mm [color="Blue (470nm)" current=0.030 package="3 mm [THT]"]
  LED10 = LED - 3mm [color="Blue (470nm)" current=0.030 package="3 mm [THT]"]
  LED11 = LED - 3mm [color="Blue (470nm)" current=0.030 package="3 mm [THT]"]
  LED12 = LED - 3mm [color="Red (633nm)" current=0.030 package="3 mm [THT]"]
  LED13 = LED - 3mm [color="Red (633nm)" current=0.030 package="3 mm [THT]"]
  LED14 = LED - 3mm [color="Red (633nm)" current=0.030 package="3 mm [THT]"]
  LED15 = LED - 3mm [color="Red (633nm)" current=0.030 package="3 mm [THT]"]
  LED16 = LED - 3mm [color="Red (633nm)" current=0.030 package="3 mm [THT]"]
  LED17 = LED - 3mm [color="Red (633nm)" current=0.030 package="3 mm [THT]"]
  LED18 = LED - 3mm [color="Green (565nm)" current=0.030 package="3 mm [THT]"]
  LED19 = LED - 3mm [color="Green (565nm)" current=0.030 package="3 mm [THT]"]
  LED20 = LED - 3mm [color="Green (565nm)" current=0.030 package="3 mm [THT]"]
  LED21 = LED - 3mm [color="Green (565nm)" current=0.030 package="3 mm [THT]"]
  LED22 = LED - 3mm [color="Green (565nm)" current=0.030 package="3 mm [THT]"]
  LED23 = LED - 3mm [color="Green (565nm)" current=0.030 package="3 mm [THT]"]
  LED24 = LED - 3mm [color="Yellow (585nm)" current=0.030 package="3 mm [THT]"]
  LED25 = LED - 3mm [color="Yellow (585nm)" current=0.030 package="3 mm [THT]"]
  LED26 = LED - 3mm [color="Yellow (585nm)" current=0.030 package="3 mm [THT]"]
  LED27 = LED - 3mm [color="Yellow (585nm)" current=0.030 package="3 mm [THT]"]
  LED28 = LED - 3mm [color="Yellow (585nm)" current=0.030 package="3 mm [THT]"]
  LED29 = LED - 3mm [color="Yellow (585nm)" current=0.030 package="3 mm [THT]"]
  LED30 = LED - 3mm [color="White (8000K)" current=0.030 package="3 mm [THT]"]
  LED31 = LED - 3mm [color="White (8000K)" current=0.030 package="3 mm [THT]"]
  LED32 = LED - 3mm [color="White (8000K)" current=0.030 package="3 mm [THT]"]
  LED33 = LED - 3mm [color="White (8000K)" current=0.030 package="3 mm [THT]"]
  LED34 = LED - 3mm [color="White (8000K)" current=0.030 package="3 mm [THT]"]
  LED35 = LED - 3mm [color="White (8000K)" current=0.030 package="3 mm [THT]"]
  M1 = MAX7219 8x8 single Led Matrix Module
  元件2 = Passive Buzzer
  Part3 = Bluetooth HC-05 Macho
  TTP223B2 = TTP223B Capacitive Touch Sensor Module [part_number="Touch sensor"]

nets:
  N1: 元件1.D8, Part3.RXD
  N2: 元件1.D9_PWM, Part3.TXD
  N3: 元件1.D10_PWM/SS, M1.O-CS
  N4: 元件1.D11_PWM/MOSI, M1.O-CLK
  N5: 元件1.D12/MISO, M1.O-DOUT
  N6: 元件1.D13/SCK, 元件2.S
  GND: 元件1.GND, LED1.cathode, LED2.cathode, LED3.cathode, LED4.cathode, LED5.cathode, LED6.cathode, LED7.cathode, LED8.cathode, LED9.cathode, LED10.cathode, LED11.cathode, LED12.cathode, LED13.cathode, LED14.cathode, LED15.cathode, LED16.cathode, LED17.cathode, LED18.cathode, LED19.cathode, LED20.cathode, LED21.cathode, LED22.cathode, LED23.cathode, LED24.cathode, LED25.cathode, LED26.cathode, LED27.cathode, LED28.cathode, LED29.cathode, LED30.cathode, LED31.cathode, LED32.cathode, LED33.cathode, LED34.cathode, LED35.cathode, M1.I-GND, M1.O-GND, 元件2.GND, Part3.GND, TTP223B2.GND
  N7: 元件1.D2, TTP223B2.SIG
  N8: 元件1.D3_PWM, LED2.anode, LED6.anode, LED7.anode, LED8.anode, LED9.anode, LED10.anode, LED11.anode
  N9: 元件1.D4, LED1.anode, LED12.anode, LED13.anode, LED14.anode, LED15.anode, LED16.anode, LED17.anode
  N10: 元件1.D5_PWM, LED3.anode, LED18.anode, LED19.anode, LED20.anode, LED21.anode, LED22.anode, LED23.anode
  N11: 元件1.D6_PWM, LED4.anode, LED24.anode, LED25.anode, LED26.anode, LED27.anode, LED28.anode, LED29.anode
  N12: 元件1.D7, LED5.anode, LED30.anode, LED31.anode, LED32.anode, LED33.anode, LED34.anode, LED35.anode
  VCC: 元件1.5V, M1.I-VCC, M1.O-VCC, 元件2.NC, Part3.VCC, TTP223B2.VCC

notes:
  [8x8矩阵显示]
  TM7219
  5种 RGB 灯条
  触摸开关 TTP-223
  JDY-16 蓝牙模块
  蜂鸣器 KY-006

custom parts:
  MAX7219 8x8 single Led Matrix Module: Description: MAX7219 8x8 LedMatrix single Red Module Dimensions: 32x32mm Documents:
  TTP223B Capacitive Touch Sensor Module: The TTP223B capacitive touch sensor module uses the TTP223B IC. The appropriate voltage is approximately 2 to 5.5 volts.

// code stored in the sketch: jump_heart.ino
#include "SCoop.h"
#include <SoftwareSerial.h>
#define Sortware_TX 8
#define Sortware_RX 9

byte read_data, bt_data;
SoftwareSerial BT_model(Sortware_RX, Sortware_TX);

int ANIMDELAY = 120;  // animation delay, deafault value is 100
int INTENSITYMIN = 0; // minimum brightness, valid range [0,15]
int INTENSITYMAX = 8; // maximum brightness, valid range [0,15]
 
int DIN_PIN = 12;      // data in pin
int CS_PIN = 10;       // load (CS) pin
int CLK_PIN = 11;      // clock pin

// Sensor
int LedBlue = 3;
int LedRed = 4;
int LedGreen = 5;
int LedYellow = 6;
int LedWhite = 7;
int Sensor = 2;

// global value
int boot_sign = 0;  // ????
int animation_switch = 0;   // ????????
int which_light_is_lighting = LedWhite;   // ??????
int setTime = 0; // ????
 
// MAX7219 registers
byte MAXREG_DECODEMODE = 0x09;
byte MAXREG_INTENSITY  = 0x0a;
byte MAXREG_SCANLIMIT  = 0x0b;
byte MAXREG_SHUTDOWN   = 0x0c;
byte MAXREG_DISPTEST   = 0x0f;
 
const unsigned char heart[] = {
  B01100110,
  B11111111,
  B11111111,
  B11111111,
  B01111110,
  B00111100,
  B00011000,
  B00000000
};

const unsigned char Square[] = {
  B11111111,
  B11000011,
  B10100101,
  B10011001,
  B10011001,
  B10100101,
  B11000011,
  B11111111
};
 
const unsigned char star[] = {
  B00001000,
  B00011000,
  B01111110,
  B00111100,
  B00111000,
  B00101100,
  B01000010,
  B00000000
};

const unsigned char triple[] = {
  B00001000,
  B00011000,
  B00111100,
  B11111110,
  B01111111,
  B00111100,
  B00011000,
  B00010000,
};

const unsigned char monster[] = {
  B00100100,
  B01100110,
  B01111110,
  B10100101,
  B10100101,
  B10000001,
  B01011010,
  B00100100,
};

const unsigned char ghost[] = {
  B00111100,
  B01000010,
  B10100101,
  B10000001,
  B10111101,
  B10000001,
  B01010101,
  B00101010,
};

const unsigned char none[] = {
  B00000000,
  B00000000,
  B00000000,
  B00000000,
  B00000000,
  B00000000,
  B00000000,
	B00000000,
};

defineTask(TaskBT);
defineTask(TaskRunTouchSensor);
defineTask(TaskOnLight);
defineTask(TaskAnimationOnLED);
defineTask(TaskSetClock);

  B00000000
};

defineTask(TaskBT);
defineTask(TaskRunTouchSensor);
defineTask(TaskOnLight);
defineTask(TaskAnimationOnLED);
defineTask(TaskSetClock);

void setup () {
  mySCoop.start();
}
 
void loop () {
  yield();
}

// ????
void TaskBT::setup() {
  Serial.begin(9600);
  BT_model.begin(9600);
}

void TaskBT::loop() {
  if (BT_model.available()) {
    bt_data = BT_model.read();
    delay(2);
    int com = bt_data;
    
    if (boot_sign == 0 && com == 0x01) {
      // ??
      boot_sign = 1;
    } else if (boot_sign == 1 && com == 0x00) {
      // ??
      Serial.println(bt_data);
      boot_sign = 0;
      changeAnimation(0x00);
    } else if (boot_sign == 1) {
      // ????
      if (bt_data >= 0x90 && bt_data <= 0x94) {
        if (bt_data == 0x91) {setTime = 15;}
        else if (bt_data == 0x92) {setTime = 30;}
        else if (bt_data == 0x93) {setTime = 105;}
        else if (bt_data == 0x94) {setTime = 130;}
        else {setTime = 0;}
        tone(13, 4000, 200);
      } else if (bt_data < 0x08 || bt_data > 0x15) {
        which_light_is_lighting = bt_data; // ????? ??
      } else { // ????
        if (bt_data == 0x14) {
          animation_switch = 1; 
          changeAnimation(0x08);
        } else if (bt_data == 0x15) {
          animation_switch = 0; 
          changeAnimation(0x00);
        }else {
          changeAnimation(bt_data);
        }
      }
    } else {
      boot_sign = 0;
    }
  }
  if (Serial.available() > 0) {
    read_data = Serial.read();
    delay(2);
    BT_model.write(read_data);
  }
}

// ????
void TaskSetClock::setup() {
  setTime = 0;
}

void TaskSetClock::loop() {
  if (boot_sign > 0 && setTime > 0) {
    if (setTime <= 1) { boot_sign = 0; }
    setTime = setTime - 1;
    delay(1000);
  } else {
    
  }  
}

// ??????
void TaskRunTouchSensor::setup() {
  initTouchSenor();
}

void TaskRunTouchSensor::loop() {
  loopTouchSenor();
}

// LED???
void TaskOnLight::setup() {
  initLedLight();
}

void TaskOnLight::loop() {
  if (boot_sign == 1) {
    switch(which_light_is_lighting) {
      case 2: {
        // ???
        for (int i=3; i<=7; i++) {
          ShokeLight(i, true);
          delay(100);
        }
        break;
      }
      case 3 : {
        // ??
        ShokeLight(LedBlue, true); break;
      }
      case 4 : {
        // ??
        ShokeLight(LedRed, true); break;
      }
      case 5 : {
        // ??
        ShokeLight(LedGreen, true); break;
      }
      case 6 : {
        // ??
        ShokeLight(LedYellow, true); break;
      }
      // ????
      default : {
        ShokeLight(LedWhite, true); 
        break;
      }
    }
  } else {
    ShokeLight(1, false);
  }
}

// 8x8 ????
void TaskAnimationOnLED::setup() {
  initSetupDraw();  
}

void TaskAnimationOnLED::loop() {
  loopAnimation();
}

void setRegistry(byte reg, byte value) {
  digitalWrite(CS_PIN, LOW);
 
  putByte(reg);   // specify register
  putByte(value); // send data
 
  digitalWrite(CS_PIN, LOW);
  digitalWrite(CS_PIN, HIGH);
}
 
void putByte(byte data) {
  byte i = 8;
  byte mask;
  while (i > 0)
  {
    mask = 0x01 << (i - 1);        // get bitmask
    digitalWrite( CLK_PIN, LOW);   // tick
    if (data & mask)               // choose bit
      digitalWrite(DIN_PIN, HIGH); // send 1
    else
      digitalWrite(DIN_PIN, LOW);  // send 0
    digitalWrite(CLK_PIN, HIGH);   // tock
    --i;                           // move to lesser bit
  }
}

void initSetupDraw() {
  pinMode(DIN_PIN, OUTPUT);
  pinMode(CLK_PIN, OUTPUT);
  pinMode(CS_PIN, OUTPUT);
 
  // initialization of the MAX7219
  setRegistry(MAXREG_SCANLIMIT, 0x07);
  setRegistry(MAXREG_DECODEMODE, 0x00);  // using an led matrix (not digits)
  setRegistry(MAXREG_SHUTDOWN, 0x01);    // not in shutdown mode
  setRegistry(MAXREG_DISPTEST, 0x00);    // no display test
  setRegistry(MAXREG_INTENSITY, 0x0f & INTENSITYMIN);
 
  // draw hearth
  changeAnimation(0x00);
}

void loopAnimation() {
    // second beat
  setRegistry(MAXREG_INTENSITY, 0x0f & INTENSITYMAX);
  delay(ANIMDELAY);
  
  // switch off
  setRegistry(MAXREG_INTENSITY, 0x0f & INTENSITYMIN);
  delay(ANIMDELAY);
  
  // second beat
  setRegistry(MAXREG_INTENSITY, 0x0f & INTENSITYMAX);
  delay(ANIMDELAY);
  
  // switch off
  setRegistry(MAXREG_INTENSITY, 0x0f & INTENSITYMIN);
  delay(ANIMDELAY*6);
}

// 8x8 ??????
void changeAnimation(byte led) {
  // ??????????????
    if (animation_switch != 0) {
      if (led == 0x08) {
      for (int i = 1; i<=8; i++) {
          setRegistry(i, monster[i-1]);
        }
    } else if (led == 0x09) {
      for (int i = 1; i<=8; i++) {
          setRegistry(i, Square[i-1]);
        }
    } else if (led == 0x10) {
      for (int i = 1; i<=8; i++) {
          setRegistry(i, heart[i-1]);
        }
    } else if ( led == 0x11) {
      for (int i = 1; i<=8; i++) {
          setRegistry(i, ghost[i-1]);
        }
    } else if ( led == 0x12) {
      for (int i = 1; i<=8; i++) {
          setRegistry(i, triple[i-1]);
        }
    } else if ( led == 0x13) {
      for (int i = 1; i<=8; i++) {
          setRegistry(i, star[i-1]);
        }
    } else {
      for (int i = 1; i<=8; i++) {
          setRegistry(i, none[i-1]);
        }
    }
  } else {
    for (int i = 1; i<=8; i++) {
      setRegistry(i, none[i-1]);
    }
  }
}

void initTouchSenor() {
  pinMode(Sensor, INPUT);
  Serial.begin(9600);
}

void loopTouchSenor() {
  boot_sign = boot_sign ^ digitalRead(Sensor);
  if (boot_sign == 0) {
    changeAnimation(0x00);
  }
  Serial.println(boot_sign);
}

// ?????LED?
void initLedLight() {
  pinMode(LedBlue, OUTPUT);
  pinMode(LedRed, OUTPUT);
  pinMode(LedGreen, OUTPUT);
  pinMode(LedYellow, OUTPUT);
  pinMode(LedWhite, OUTPUT);
}

void ShokeLight(int light, bool open) {
  for (int i = 3; i<=7; i++) {
    if (light == i && open) {
      digitalWrite(i, HIGH);
    } else {
      digitalWrite(i, LOW);
    }
  }
}
